# Fritzing sketch clock Watch (saved by Fritzing 0.9.4)
circuit board: 8.46667cm x 5.64444cm
breadboards: 1

parts:
  Part1 = Arduino Uno (Rev3) - ICSP
  mode = Pushbutton [package="[SMD]"]
  plus = Pushbutton [package="[SMD]"]
  minus = Pushbutton [package="[SMD]"]
  select = Pushbutton [package="[SMD]"]
  start = Pushbutton [package="[SMD]"]
  R3 = Resistor [tolerance=±5% resistance=220 package="0402 [SMD]"]
  R4 = Resistor [tolerance=±5% resistance=220 package="0402 [SMD]"]
  MH-Real-Time_Clock_Module_3 = RTC_DS1302_module
  LCD2 = LCD screen
  LCM1602_IIC2 = LCM1602 IIC [part_number="LCM1602 IIC" chip_label="LCM1602 IIC" package="DIP (Dual Inline) [THT]"]
  R6 = Resistor [tolerance=±5% resistance=220 package="0402 [SMD]"]
  R7 = Resistor [tolerance=±5% resistance=220 package="0402 [SMD]"]
  J1 = Piezo Speaker
  R8 = Resistor [tolerance=±5% resistance=100 package=THT]
  AM1 = AM2302 Humidity and Temperature Sensor
  R9 = Resistor [tolerance=±5% resistance=220 package="0402 [SMD]"]

nets:
  N1: Part1.A4/SDA, LCM1602_IIC2.SDA
  N2: Part1.A5/SCL, LCM1602_IIC2.SCL
  VCC: Part1.5V, mode.Pin_3, mode.Pin_4, plus.Pin_3, plus.Pin_4, minus.Pin_3, minus.Pin_4, select.Pin_3, select.Pin_4, start.Pin_3, start.Pin_4, MH-Real-Time_Clock_Module_3.VCC, LCM1602_IIC2.VCC, AM1.VDD
  GND: Part1.GND, R3.Pin_1, R4.Pin_1, MH-Real-Time_Clock_Module_3.GND, LCM1602_IIC2.GND, R6.Pin_1, R7.Pin_1, J1.pin1, AM1.GND, R9.Pin_1
  N3: Part1.D8, MH-Real-Time_Clock_Module_3.RST
  N4: Part1.D9_PWM, R8.Pin_1
  N5: Part1.D11_PWM/MOSI, start.Pin_1, start.Pin_2, R9.Pin_0
  N6: Part1.D12/MISO, minus.Pin_1, minus.Pin_2, R3.Pin_0
  N7: Part1.D13/SCK, AM1.DATA
  N8: Part1.D2, mode.Pin_1, mode.Pin_2, R7.Pin_0
  N9: Part1.D3_PWM, plus.Pin_1, plus.Pin_2, R4.Pin_0
  N10: Part1.D4, select.Pin_1, select.Pin_2, R6.Pin_0
  N11: Part1.D6_PWM, MH-Real-Time_Clock_Module_3.CLK
  N12: Part1.D7, MH-Real-Time_Clock_Module_3.DAT
  VSS: LCD2.VSS, LCM1602_IIC2.VSS
  VDD: LCD2.VDD, LCM1602_IIC2.VDD
  N13: LCD2.V0, LCM1602_IIC2.V0
  N14: LCD2.RS, LCM1602_IIC2.RS
  N15: LCD2.R/W, LCM1602_IIC2.RW
  N16: LCD2.E, LCM1602_IIC2.E
  N17: LCD2.DB0, LCM1602_IIC2.D0
  N18: LCD2.DB1, LCM1602_IIC2.D1
  N19: LCD2.DB2, LCM1602_IIC2.D2
  N20: LCD2.DB3, LCM1602_IIC2.D3
  N21: LCD2.DB4, LCM1602_IIC2.D4
  N22: LCD2.DB5, LCM1602_IIC2.D5
  N23: LCD2.DB6, LCM1602_IIC2.D6
  N24: LCD2.DB7, LCM1602_IIC2.D7
  N25: LCD2.LED+, LCM1602_IIC2.A
  N26: LCD2.LED-, LCM1602_IIC2.K
  N27: LCM1602_IIC2.LED_A, LCM1602_IIC2.LED_B

custom parts:
  RTC_DS1302_module: Arduino module DS1302 SPI Real Time Clock
  LCM1602 IIC: I2C-Module to use a 1602 or 2004 LCD on with the wire.h libory Serial LCD Modul

// code stored in the sketch: code.ino
#include <DHT.h>
#include <LiquidCrystal_I2C.h>
#include <Wire.h>
#include <virtuabotixRTC.h>


// Constants
#define DHT11_PIN 13
#define DHTPIN 13         // what pin we're connected to
#define DHTTYPE DHT22     // DHT 22  (AM2302)
DHT dht(DHTPIN, DHTTYPE); //// Initialize DHT sensor for normal 16mhz Arduino


// Variables
int chk;
float hum;  // Stores humidity value
float temp; // Stores temperature value


boolean buttonActive = false;
boolean longPressActive = false;


long buttonTimer = 0;
long longPressTime = 400;


// Creation of the Real Time Clock Object
virtuabotixRTC myRTC(6, 7, 8);
const int buzzer = 9;
const int buttonPin1 = 2;
const int buttonPin2 = 3;
const int buttonPin3 = 4;
const int buttonPin4 = 12;
const int buttonPin5 = 11;


LiquidCrystal_I2C lcd(0x27, 16, 2);
int buttonState1 = 0;
int buttonState2 = 0;
int buttonState3 = 0;
int buttonState4 = 0;
int buttonState5 = 0;


int hours = 10;
int minute = 0;


int secondsSet = 0;
int minutesSet = 0;
int hoursSet = 0;
int monthSet = 0;
int dayMonthSet = 0;
int dayWeekSet = 0;


int timerMin = 0;
int timerSec = 0;


int clicks = 0;
int clicks2 = 0;
int clicks3 = 0;
int clicks4 = 0;


int timerOn = 0;


String hourTime;
String secondTime;
String minuteTime;


String dayofmonthTime;
String monthTime;


String hoursSetDisplay;
String minutesSetDisplay;
String secondsSetDisplay;


String daySetDisplay;
String monthSetDisplay;


String dayWeekDisplay;


String timerSecDisplay;
String timerMinDisplay;


String alarmHourDisplay;
String alarmMinuteDisplay;




int screens = 1;


bool alarmToggle = true;
bool timerToggle = true;


int x = 0;
int newButtonState;



    
unsigned long previousMillis1 = 0;
unsigned long interval1 = 1000UL;


void setup() {
  Serial.begin(9600);
  pinMode(buzzer, OUTPUT);
  // seconds, minutes, hours, day of the week, day of the month, month, year
  myRTC.setDS1302Time(0, 0, 0, 1, 1, 1, 2021);
  myRTC.updateTime();
  dayMonthSet = myRTC.dayofmonth;
  monthSet = myRTC.month;
  secondsSet = myRTC.seconds;
  minutesSet = myRTC.minutes;
  hoursSet = myRTC.hours;
  dayWeekSet = myRTC.dayofweek;
  pinMode(buttonPin1, INPUT);
  pinMode(buttonPin2, INPUT);
  pinMode(buttonPin3, INPUT);
  pinMode(buttonPin4, INPUT);
  int buttonState1 = 0;
  int buttonState2 = 0;
  int buttonState3 = 0;
  lcd.begin();
  dht.begin();


  lcd.backlight();
  lcd.clear();
  lcd.setCursor(0, 0);
  lcd.print("Daniel Alarm watch");
  lcd.clear();
}


void loop() {
  screensSelect:
  myRTC.updateTime();
  if (screens == 1) {
    screen_1();
  } else if (screens == 2) {
    screen_2();
  } else if (screens == 3) {
    screen_3();
  } else if (screens == 4) {
    set_time();
  } else if (screens == 5) {
    set_date();
  } else if (screens == 6){
    set_day();
  }
    if (millis() - previousMillis1 > interval1) {
      // save the last time you blinked the LED
      previousMillis1 += interval1;  
      if(timerOn == 1){
        if(timerMin == 0 && timerSec == 0 && timerToggle){
            timerOn = 0;
            Serial.println("alarm");
            delay(170);
            for (int i = 0; i < 255; i++) {
              myRTC.updateTime();
              analogWrite(buzzer, i);
              buttonState1 = digitalRead(buttonPin1);
              if (buttonState1 == HIGH) {
                timerToggle = false;
                noTone(buzzer);
                delay(170);
                break;
              }
              delay(10); // wait 10 milliseconds to repeat
            }
            for (int i = 255; i > 0; i--) { // do this 255 times
              analogWrite(buzzer, i); // lower the voltage sent out of the pin by 1
              myRTC.updateTime();
              buttonState1 = digitalRead(buttonPin1);
              if (buttonState1 == HIGH) {
                timerToggle = false;
                noTone(buzzer);
                delay(170);
                break;
              }
              delay(10); // wait 10 milliseconds to repeat
            }
            noTone(buzzer);
        }else{
          timerSec -= 1;
          if(timerSec < 0){
            if(timerMin != 0){
              timerMin-=1;
             }
            timerSec = 59;
          }
        }
      }
    }
}
void startDown(){ 
  if (buttonState1 == HIGH) {
    timerOn = 0;
    delay(200);
  }
  delay(1000);
  timerSec -= 1;
  if(timerSec < 0){
    if(timerMin != 0){
      timerMin-=1;
    }
    timerSec = 59;
  }
}
void fixSetTime() {
  if (hoursSet < 10) {
    hoursSetDisplay = String(0) + String(hoursSet);
  } else if (hoursSet >= 10) {
    hoursSetDisplay = String(hoursSet);
  }
  if (minutesSet < 10) {
    minutesSetDisplay = String(0) + String(minutesSet);
  } else if (minutesSet >= 10) {
    minutesSetDisplay = String(minutesSet);
  }


  if (secondsSet < 10) {
    secondsSetDisplay = String(0) + String(secondsSet);
  } else if (secondsSet >= 10) {
    secondsSetDisplay = String(secondsSet);
  }
}
void fixSetDate() {
  if (dayMonthSet < 10) {
    daySetDisplay = String(0) + String(dayMonthSet);
  } else if (dayMonthSet >= 10) {
    daySetDisplay = String(dayMonthSet);
  }
  if (monthSet < 10) {
    monthSetDisplay = String(0) + String(monthSet);
  } else if (monthSet >= 10) {
    monthSetDisplay = String(monthSet);
  }
}
void fixTimeDate() {
  if (myRTC.hours < 10) {
    hourTime = String(0) + String(myRTC.hours);
  } else if (myRTC.hours >= 10) {
    hourTime = String(myRTC.hours);
  }
  if (myRTC.minutes < 10) {
    minuteTime = String(0) + String(myRTC.minutes);
  } else if (myRTC.minutes >= 10) {
    minuteTime = String(myRTC.minutes);
  }
  if (myRTC.seconds < 10) {
    secondTime = String(0) + String(myRTC.seconds);
  } else if (myRTC.seconds >= 10) {
    secondTime = String(myRTC.seconds);
  }
  if (myRTC.dayofmonth < 10) {
    dayofmonthTime = String(0) + String(myRTC.dayofmonth);
  } else if (myRTC.dayofmonth >= 10) {
    dayofmonthTime = String(myRTC.dayofmonth);
  }
  if (myRTC.month < 10) {
    monthTime = String(0) + String(myRTC.month);
  } else if (myRTC.seconds >= 10) {
    monthTime = String(myRTC.month);
  }
  // alarm
  if (hours < 10) {
    alarmHourDisplay = String(0) + String(hours);
  } else if (hours >= 10) {
    alarmHourDisplay = String(hours);
  }
  if (minute < 10) {
    alarmMinuteDisplay = String(0) + String(minute);
  } else if (minute >= 10) {
    alarmMinuteDisplay = String(minute);
  }
  switch(dayWeekSet){
    case 1:
      dayWeekDisplay = "Sun";
      break;
    case 2:
      dayWeekDisplay = "Mon";
      break;
    case 3:
      dayWeekDisplay = "Tue";
      break;
    case 4:
      dayWeekDisplay = "Wed";
      break;
    case 5:
      dayWeekDisplay = "Thu";
      break;
    case 6:
      dayWeekDisplay = "Fri";
      break;
    case 7:
      dayWeekDisplay = "Sat";
      break;
  }
}
void fixTimer(){
  if (timerMin < 10) {
    timerMinDisplay = String(0) + String(timerMin);
  } else if (timerMin >= 10) {
    timerMinDisplay = String(timerMin);
  }
  if (timerSec < 10) {
    timerSecDisplay = String(0) + String(timerSec);
  } else if (timerSec >= 10) {
    timerSecDisplay = String(timerSec);
  }
}
void screen_1() {
  fixTimeDate();
  if (myRTC.hours == hours && myRTC.minutes == minute && alarmToggle) {
    delay(170);
    lcd.clear();
    lcd.setCursor(0, 0);
    lcd.print("Its: ");
    lcd.print(alarmHourDisplay);
    lcd.print(":");
    lcd.print(alarmMinuteDisplay);
    fixTimeDate();
    for (int i = 0; i < 255; i++) {
      myRTC.updateTime();
      analogWrite(buzzer, i);
      buttonState1 = digitalRead(buttonPin1);
      if (buttonState1 == HIGH) {


        alarmToggle = false;
        noTone(buzzer);
        delay(170);
        break;
      }
      delay(10); // wait 10 milliseconds to repeat
    }


    for (int i = 255; i > 0; i--) { // do this 255 times
      analogWrite(buzzer, i); // lower the voltage sent out of the pin by 1
      myRTC.updateTime();
      buttonState1 = digitalRead(buttonPin1);
      if (buttonState1 == HIGH) {
        alarmToggle = false;
        noTone(buzzer);
        delay(170);
        break;
      }
      delay(10); // wait 10 milliseconds to repeat
    }
    buttonState1 = digitalRead(buttonPin1);
    if (buttonState1 == HIGH) {
      alarmToggle = false;
      noTone(buzzer);
      delay(170);
    }
    noTone(buzzer);
  } else {


    if (myRTC.minutes - 1 == minute) {
      alarmToggle = true;
    }
    temp = dht.readTemperature();
    lcd.setCursor(0, 0);
    lcd.print(hourTime);
    lcd.print(":");
    lcd.print(minuteTime);
    lcd.print(".");
    lcd.print(secondTime);
    lcd.print("  ");
    lcd.print("T:");
    lcd.print(temp,0);
    lcd.print((char)223);
    lcd.print("C");
    lcd.setCursor(0, 1);
    lcd.print(" ");
    lcd.print(dayWeekDisplay);
    lcd.print(" ");
    lcd.print(dayofmonthTime);
    lcd.print("/");
    lcd.print(monthTime);
    lcd.print("/");
    lcd.print(myRTC.year);
    lcd.print("  ");
    
  }
  if (digitalRead(buttonPin1) == HIGH) {


    if (buttonActive == false) {


      buttonActive = true;
      buttonTimer = millis();
    }


    if ((millis() - buttonTimer > longPressTime) &&
        (longPressActive == false)) {


      longPressActive = true;
      screens = 4;
      
    }


  } else {


    if (buttonActive == true) {


      if (longPressActive == true) {


        longPressActive = false;


      } else {


        delay(170);
        lcd.clear();
        screens = 2;
   
      }


      buttonActive = false;
    }
  }
}
void screen_2() {
  lcd.blink();
  int i = 1;
  
  buttonState3 = digitalRead(buttonPin3);
  if (buttonState3 == HIGH) {


    if (x == 0) {
      // Toggle on
      x = 1;
      lcd.setCursor(3, 1);
    } else {
      // Toggle off
      lcd.setCursor(0, 1);
      x = 0;
    }
  }
  // add time
  buttonState2 = digitalRead(buttonPin2);
  if (buttonState2 == HIGH) {
    //hours up
    if (x == 0) {
      hours += 1;
      if (hours >= 24) {
        hours = 0;
      }
    }
    //minutes up
    if (x == 1) {
      minute += 1;
      if (minute >= 60) {
        minute = 0;
      }
    }
  }
  buttonState4 = digitalRead(buttonPin4);
  //houra down
  if (buttonState4 == HIGH) {
    if (x == 0) {
      hours -= 1;
      if (hours < 0) {
        hours = 23;
      }
    }
    //minute down
    if (x == 1) {
      minute -= 1;
      if (minute < 0) {
        minute = 59;
      }
    }
  }
  //print the alarm time:
  fixTimeDate();
  lcd.setCursor(0, 0);
  lcd.print("Alarm Time:");
  lcd.setCursor(0, 1);
  lcd.print(alarmHourDisplay);
  lcd.print(":");
  lcd.print(alarmMinuteDisplay);
  lcd.print("  ");
  lcd.blink();
  if (x == 0) {
      // Toggle on
      lcd.setCursor(0, 1);
    } else {
      // Toggle off
      lcd.setCursor(3, 1);
    }
  //next screen
  buttonState1 = digitalRead(buttonPin1);
  if (buttonState1 == HIGH) {
    delay(200);
    lcd.clear();
    screens = 3;
  }
  delay(170);
}


void screen_3() {
  //turn on timer:
  buttonState5 = digitalRead(buttonPin5);
  if (buttonState5 == HIGH) {   
    if (clicks4 == 1) {
      timerOn = 0;
      clicks4 = 0;
    }else{
      timerOn = 1;
      clicks4 +=1;
    }
  }
  //select min/sec
  buttonState3 = digitalRead(buttonPin3);
  if (buttonState3 == HIGH) {
    if (clicks3 == 1) {
      clicks3 = 0;
    } else {
      clicks3 += 1;
    }
  }
  buttonState2 = digitalRead(buttonPin2);
  if (buttonState2 == HIGH) {
    //min up
    if (clicks3 == 0) {
      lcd.setCursor(0, 1);
      timerMin += 1;
      lcd.setCursor(0, 1);
      if (timerMin >= 100) {
        timerMin = 0;
      }
    }
    //sec up
    if (clicks3 == 1) {
      lcd.setCursor(3, 1);
      timerSec += 1;
      lcd.setCursor(3, 1);
      if (timerSec >= 60) {
        timerSec = 0;
      }
    }
  }
  buttonState4 = digitalRead(buttonPin4);
  if (buttonState4 == HIGH) {
    //min down
    if (clicks3 == 0) {
      lcd.setCursor(0, 1);
      timerMin -= 1;
      lcd.setCursor(0, 1);
      if (timerMin < 0) {
        timerMin = 99;
      }
    }
    //sec down
    if (clicks3 == 1) {
      lcd.setCursor(3, 1);
      timerSec -= 1;
      lcd.setCursor(3, 1);
      if (timerSec < 0) {
        timerSec = 59;
      }
    }
  }
  //print timer
  fixTimer();
  lcd.setCursor(0,0);
  lcd.print("Timer:");
  lcd.setCursor(0,1);
  lcd.print(timerMinDisplay);
  lcd.print(":");
  lcd.print(timerSecDisplay);
  lcd.print("   ");
  if (clicks3 == 0) {
    lcd.setCursor(0, 1);
  }
  if (clicks3 == 1) {
    lcd.setCursor(3, 1);
  }
  //next screen
  buttonState1 = digitalRead(buttonPin1);
  if (buttonState1 == HIGH) {
    delay(200);
    lcd.clear();
    screens = 1;
  }  
  delay(170);
}
void set_time() {
  lcd.blink();
  delay(170);
  hoursSet = myRTC.hours;
  minutesSet = myRTC.minutes;
  secondsSet = myRTC.seconds;
  fixSetTime();
  //next screen
  buttonState1 = digitalRead(buttonPin1);
  if (buttonState1 == HIGH) {
    delay(200);
    screens = 5;
  }
  if (clicks == 0) {
    lcd.setCursor(0, 1);
  }
  if (clicks == 1) {
    lcd.setCursor(3, 1);
  }
  if (clicks == 2) {
    lcd.setCursor(6, 1);
  }
  //select hours/min/sec
  buttonState3 = digitalRead(buttonPin3);
  if (buttonState3 == HIGH) {
    if (clicks == 2) {
      clicks = 0;
    } else {
      clicks += 1;
    }
  }
  buttonState2 = digitalRead(buttonPin2);
  if (buttonState2 == HIGH) {
    //hours up
    if (clicks == 0) {
      lcd.setCursor(0, 1);
      hoursSet += 1;
      lcd.setCursor(0, 1);
      if (hoursSet >= 24) {
        hoursSet = 0;
      }
    }
    if (clicks == 1) {
      //min up
      lcd.setCursor(3, 1);
      minutesSet += 1;
      lcd.setCursor(3, 1);
      if (minutesSet >= 60) {
        minutesSet = 0;
      }
    }
    if (clicks == 2) {
      //sec up
      lcd.setCursor(6, 1);
      secondsSet += 1;
      lcd.setCursor(6, 1);
      if (secondsSet >= 60) {
        secondsSet = 0;
      }
    }
  }
  buttonState4 = digitalRead(buttonPin4);
  if (buttonState4 == HIGH) {
    //hours down
    if (clicks == 0) {
      lcd.setCursor(0, 1);
      hoursSet -= 1;
      lcd.setCursor(0, 1);
      if (hoursSet < 0) {
        hoursSet = 23;
      }
    }
    //min down
    if (clicks == 1) {
      lcd.setCursor(3, 1);
      minutesSet -= 1;
      lcd.setCursor(3, 1);
      if (minutesSet < 0) {
        minutesSet = 59;
      }
    }
    //sec down
    if (clicks == 2) {
      lcd.setCursor(6, 1);
      secondsSet -= 1;
      lcd.setCursor(6, 1);
      if (secondsSet < 0) {
        secondsSet = 59;
      }
    }
  }
  //print set time
  lcd.setCursor(0, 0);
  lcd.print("Set Time:       ");
  lcd.setCursor(0, 1);
  lcd.print(hoursSetDisplay);
  lcd.print(":");
  lcd.print(minutesSetDisplay);
  lcd.print(":");
  lcd.print(secondsSetDisplay);
  lcd.print("        ");
  if (clicks == 0) {
    lcd.setCursor(0, 1);
  }
  if (clicks == 1) {
    lcd.setCursor(3, 1);
  }
  if (clicks == 2) {
    lcd.setCursor(6, 1);
  }
  // seconds, minutes, hours, day of the week, day of the month, month, year
  myRTC.setDS1302Time(secondsSet, minutesSet, hoursSet, 6, dayMonthSet, monthSet,2021);
}
void set_date() {
  dayMonthSet = myRTC.dayofmonth;
  monthSet = myRTC.month;
  
  //next screen
  buttonState1 = digitalRead(buttonPin1);
  if (buttonState1 == HIGH) {
    delay(200);
    screens = 6;
  }
  //select dayOfMonth/month
  buttonState3 = digitalRead(buttonPin3);
  if (buttonState3 == HIGH) {
    if (clicks2 == 1) {
      clicks2 = 0;
    } else {
      clicks2 += 1;
    }
  }
  buttonState2 = digitalRead(buttonPin2);
  if (buttonState2 == HIGH) {
    //add dayOfMonth
    if (clicks2 == 0) {
      lcd.setCursor(0, 1);
      dayMonthSet += 1;
      lcd.setCursor(0, 1);
      if (dayMonthSet > 30) {
        dayMonthSet = 1;
      }
    }
    //add month
    if (clicks2 == 1) {
      lcd.setCursor(3, 1);
      monthSet += 1;
      lcd.setCursor(3, 1);
      if (monthSet > 12) {
        monthSet = 1;
      }
    }
  }
  buttonState4 = digitalRead(buttonPin4);
  if (buttonState4 == HIGH) {
    //dayOfMonth down
    if (clicks2 == 0) {
      lcd.setCursor(0, 1);
      dayMonthSet -= 1;
      lcd.setCursor(0, 1);
      if (dayMonthSet < 1) {
        dayMonthSet = 30;
      }
    }
    //month down
    if (clicks2 == 1) {
      lcd.setCursor(3, 1);
      monthSet -= 1;
      lcd.setCursor(3, 1);
      if (monthSet < 1) {
        minutesSet = 12;
      }
    }
  }
  fixSetDate();
  lcd.setCursor(0, 0);
  lcd.print("Set Date:       ");
  lcd.setCursor(0, 1);
  lcd.print(daySetDisplay);
  lcd.print("/");
  lcd.print(monthSetDisplay);
  lcd.print("        ");


  if (clicks2 == 0) {
    lcd.setCursor(0, 1);
  }
  if (clicks2 == 1) {
    lcd.setCursor(3, 1);
  }


  // seconds, minutes, hours, day of the week, day of the month, month, year
  myRTC.setDS1302Time(secondsSet, minutesSet, hoursSet, 1, dayMonthSet, monthSet,2021);
  delay(170);
}
void set_day(){
  lcd.blink();
  dayWeekSet = myRTC.dayofweek;
  buttonState1 = digitalRead(buttonPin1);
  //next screen
  if (buttonState1 == HIGH) {
    delay(200);
    screens = 1;
  }
  
  //day up
  buttonState2 = digitalRead(buttonPin2);
  if (buttonState2 == HIGH) {
    lcd.setCursor(0, 1);
    dayWeekSet += 1;
    lcd.setCursor(0, 1);
    if (dayWeekSet > 7) {
      dayWeekSet = 1;
    }
  }
  //day down
  buttonState4 = digitalRead(buttonPin4);
  if (buttonState4 == HIGH) {
    lcd.setCursor(0, 1);
    dayWeekSet -= 1;
    lcd.setCursor(0, 1);
    if (dayWeekSet < 1) {
      dayWeekSet = 30;
    }
  }
  //print day
  fixTimeDate();
  lcd.setCursor(0, 0);
  lcd.print("Set Day Of Week:    ");
  lcd.setCursor(0, 1);
  lcd.print(dayWeekDisplay);
  lcd.print("    ");
  lcd.setCursor(3, 1);
  // seconds, minutes, hours, day of the week, day of the month, month, year
  myRTC.setDS1302Time(secondsSet, minutesSet, hoursSet, dayWeekSet, dayMonthSet, monthSet,2021);
  delay(170);
}
